# Fritzing sketch Node_CoDinh (saved by Fritzing 0.9.3b)
# 18650 Li-ion Battery: CC-BY Dr Kristofer Chan, King's College London/Remote-research.org

parts:
  U5 = ESP32-38PinWide [part_number=ESP32-38PinWide]
  BAT3 = 18650 Li-ion Battery [package=battery-18650]
  MT3608 = MT3608 Module
  U6 = SWITCH_SPDT [package=kps-1290]
  Solar_Panel1 = Generic Small 6V Solar Panel
  CN3791 = CN3065 Mini Solar Charger Module
  JSN-SR04T = JSN-SRO4T [package=THT]
  TP4056 = TP4056 [chip_label=TP4056 package="DIP (Dual Inline) [THT]"]
  C1 = Electrolytic Capacitor [capacitance=0.47mF voltage=16V package="0807 [SMD, electrolytic]"]
  R1 = Resistor [tolerance=±5% resistance=1k package="2010 [SMD]"]
  R2 = Resistor [tolerance=±5% resistance=2.2k package="2512 [SMD]"]

nets:
  N1: U5.GPIO11, MT3608.pin4, JSN-SR04T.pin1, C1.-, R2.Pin_0
  N2: U5.VIN, U6.O, JSN-SR04T.pin4
  N3: U5.GPIO5, JSN-SR04T.pin3
  N4: U5.GPIO18, R1.Pin_1, R2.Pin_1
  N5: BAT3.-, Solar_Panel1.-, CN3791.Pin_2, CN3791.Pin_10, CN3791.Pin_12, TP4056.pin5
  N6: BAT3.+, CN3791.Pin_11, TP4056.pin4
  N7: MT3608.pin1, TP4056.pin6
  N8: MT3608.pin2, TP4056.pin3
  N9: MT3608.pin3, U6.P, C1.+
  N10: Solar_Panel1.+, CN3791.Pin_1
  N11: JSN-SR04T.pin2, R1.Pin_0

custom parts:
  ESP32-38PinWide: Generic 38-Pin ESP32 with wide format (only access to one side of pins on a breadboard) based on Stephen Lilley's HiLetgo ESP-WROOM-32 ESP32 ESP-32S Development Board.
  18650 Li-ion Battery: 18650 li-ion Battery Standard 18650 battery with interactive connectors Creative Common Attribution 4.0 International (CC-BY 4.0) license. Any use of this part requires attribution of Dr Kristofer Chan, Department of Geography, King's College London. Contact kristofer.chan [at] kcl.ac.uk OR kris [at] remote-research.org for further information.
  MT3608 Module: MT3608 Boost Converter Module Links: Aerosemi MT3608 2A Step Up Converter datasheet
  CN3065 Mini Solar Charger Module: CN3791 MPPT Solar Panel Regulator Controller 6V 9V 12V 1 Zelle Lithium-Batterie Ladung Solar Panel Ladegerät board-Controller Module.
  JSN-SRO4T: JSN-SR04T Waterproof Ultrasonic Distance Measuring Module Integrated Ultrasonic Detection Module DC 5V.
  TP4056: A DIP stand-in part for whatever IC you want. With 6 pins on a 300mil dual inline package (DIP) footprint.
