# Fritzing sketch Node_DiDong (saved by Fritzing 0.9.3b)
# 18650 Li-ion Battery: CC-BY Dr Kristofer Chan, King's College London/Remote-research.org

parts:
  MPU6051 = MPU-6050 Board GY-521 [form="♀ (female)" package=THT]
  GPS3 = GPS Modul with NEO-6M
  SD_card_module3 = SD Card Module
  BAT3 = 18650 Li-ion Battery [package=battery-18650]
  M3 = MT3608 Module
  U5 = SWITCH_SPDT [package=kps-1290]
  U6 = ESP32-38PinWide [part_number=ESP32-38PinWide]
  TP4056 = TP4056 [chip_label=TP4056 package="DIP (Dual Inline) [THT]"]
  C1 = Electrolytic Capacitor [capacitance=0.47mF voltage=16V package="100 mil [THT, electrolytic]"]
  S1 = Round Pushbutton
  LED1 = smd LED [color="Red (633nm)" package="0805 [SMD]"]
  LED2 = LEDs [package=led10mm]
  R1 = Resistor [tolerance=±5% resistance=330 package="0805 [SMD]"]
  R2 = Resistor [tolerance=±5% resistance=330 package="0805 [SMD]"]

nets:
  N1: MPU6051.pin1, GPS3.VCC, SD_card_module3.+3.3, U6.3.3
  GND: MPU6051.pin2, GPS3.GND, SD_card_module3.GND, U6.GND, LED1.cathode, LED2.C
  N2: MPU6051.pin3, U6.GPIO22
  N3: MPU6051.pin4, U6.GPIO21
  N4: GPS3.TX, U6.GPIO16
  N5: GPS3.RX, U6.GPIO17
  N6: SD_card_module3.CS, U6.GPIO5
  N7: SD_card_module3.MOSI, U6.GPIO23
  N8: SD_card_module3.SCK, U6.GPIO18
  N9: SD_card_module3.MISO, U6.GPIO19
  N10: BAT3.-, TP4056.pin5
  N11: BAT3.+, TP4056.pin4
  N12: M3.pin1, TP4056.pin6
  N13: M3.pin2, U5.O
  N14: M3.pin3, U6.VIN, C1.+
  N15: M3.pin4, U6.GPIO11, C1.-, S1.leg0
  N16: U5.P, TP4056.pin3
  N17: U6.GPIO25, R1.Pin_1
  N18: U6.GPIO26, R2.Pin_1
  N19: U6.GPIO27, S1.leg1
  N20: LED1.anode, R1.Pin_0
  N21: LED2.A, R2.Pin_0

custom parts:
  MPU-6050 Board GY-521: Acelerometro y Giroscopio MPU-6050 Board GY-521
  GPS Modul with NEO-6M: GY-GPS6MV2
  SD Card Module: SD Card Module Slot Socket Reader For Arduino ARM MCU
  18650 Li-ion Battery: 18650 li-ion Battery Standard 18650 battery with interactive connectors Creative Common Attribution 4.0 International (CC-BY 4.0) license. Any use of this part requires attribution of Dr Kristofer Chan, Department of Geography, King's College London. Contact kristofer.chan [at] kcl.ac.uk OR kris [at] remote-research.org for further information.
  MT3608 Module: MT3608 Boost Converter Module Links: Aerosemi MT3608 2A Step Up Converter datasheet
  ESP32-38PinWide: Generic 38-Pin ESP32 with wide format (only access to one side of pins on a breadboard) based on Stephen Lilley's HiLetgo ESP-WROOM-32 ESP32 ESP-32S Development Board.
  TP4056: A DIP stand-in part for whatever IC you want. With 6 pins on a 300mil dual inline package (DIP) footprint.
